// Logisim project Ejemplos 1.circ as structural Verilog: 3 circuits, main circuit Ejercicio 1
module Ejercicio_1 (
  input  X1,
  input  X2,
  input  X3,
  output f
);

  wire and_1_out, and_2_out, and_3_out, not_1_out, not_2_out, not_3_out;

  not not_1 (not_1_out, X1);
  not not_2 (not_2_out, X2);
  not not_3 (not_3_out, X3);
  and and_1 (and_1_out, not_1_out, not_2_out, not_3_out);
  and and_2 (and_2_out, not_1_out, X2, X3);
  and and_3 (and_3_out, X1, X2, not_3_out);
  or or_1 (f, and_1_out, and_2_out, and_3_out);
endmodule

module Ejercicio_2 (
  input  h,
  input  X1,
  input  X2,
  output f,
  output g
);

  wire and_1_out, and_2_out, not_1_out, not_2_out, not_3_out;

  not not_1 (not_1_out, h);
  not not_2 (not_2_out, X1);
  not not_3 (not_3_out, X2);
  or or_1 (f, and_1_out, and_2_out);
  and and_1 (and_1_out, not_2_out, not_3_out);
  and and_2 (and_2_out, h, not_3_out);
  and and_3 (g, h, not_2_out, not_3_out);
endmodule

module Ejercicio_3 (
  input  A,
  input  A_2,
  input  A_3,
  input  A_4,
  input  B,
  input  A_5,
  input  B_2,
  output Not_A,
  output Not_A_2,
  output Not_A_3,
  output A___B,
  output A___B_2
);

  wire transistor_3_out;

  Transistor #(.\type ("n")) transistor_1 (.in(1'b0), .out(Not_A), .gate(A));
  Transistor transistor_2 (.in(1'b1), .out(Not_A), .gate(A));
  Transistor transistor_3 (.in(1'b0), .out(transistor_3_out), .gate(B));
  Transistor #(.\type ("n")) transistor_4 (.in(1'b1), .out(A___B), .gate(A_4));
  Transistor #(.\type ("n")) transistor_5 (.in(1'b1), .out(A___B), .gate(B));
  Transistor transistor_6 (.in(transistor_3_out), .out(A___B), .gate(A_4));
  Pull_Resistor #(.pull(1)) pull_resistor_1 (.node(Not_A_2));
  Transistor #(.\type ("n")) transistor_7 (.in(1'b0), .out(Not_A_2), .gate(A_3));
  Transistor #(.\type ("n")) transistor_8 (.in(1'b1), .out(A___B_2), .gate(A_5));
  Pull_Resistor pull_resistor_2 (.node(A___B_2));
  Transistor #(.\type ("n")) transistor_9 (.in(1'b1), .out(A___B_2), .gate(B_2));
  Transistor #(.\type ("n")) transistor_10 (.in(1'b0), .out(Not_A_3), .gate(A_2));
  Transistor #(.gate("br")) transistor_11 (.in(1'b1), .out(Not_A_3), .gate(A_2));
endmodule
