// Logisim project P3Circuitos.circ as structural Verilog: 4 circuits, main circuit Implicación
module \Implicación  (
  input  X,
  input  Y,
  output A_____B
);

  wire transistor_1_out, transistor_4_out;

  Transistor #(.\type ("n")) transistor_1 (.in(1'b0), .out(transistor_1_out), .gate(X));
  Transistor transistor_2 (.in(1'b1), .out(transistor_1_out), .gate(X));
  Transistor #(.gate("br")) transistor_3 (.in(transistor_4_out), .out(A_____B), .gate(Y));
  Transistor transistor_4 (.in(1'b0), .out(transistor_4_out), .gate(transistor_1_out));
  Transistor #(.\type ("n")) transistor_5 (.in(1'b1), .out(A_____B), .gate(transistor_1_out));
  Transistor #(.\type ("n")) transistor_6 (.in(1'b1), .out(A_____B), .gate(Y));
endmodule

module \Implicación_doble  (
  input  in_1,
  input  Y,
  output out_3
);

  wire and_1_out, and_2_out, not_1_out, not_2_out;

  not not_1 (not_1_out, in_1);
  not not_2 (not_2_out, Y);
  and and_1 (and_1_out, in_1, Y);
  and and_2 (and_2_out, not_1_out, not_2_out);
  or or_1 (out_3, and_1_out, and_2_out);

  // Notes on the sheet:
  //   X
endmodule

module Comparador_sencillo (
  input  X_1,
  input  in_2,
  input  Y_1,
  input  Y_2,
  output out_5
);

  wire and_1_out, and_2_out, and_3_out, and_4_out, and_5_out, not_1_out, not_2_out;

  not not_1 (not_1_out, Y_2);
  not not_2 (not_2_out, Y_1);
  and and_1 (and_1_out, not_2_out, not_1_out);
  and and_2 (and_2_out, X_1, in_2);
  and and_3 (and_3_out, in_2, not_2_out);
  and and_4 (and_4_out, X_1, not_1_out);
  and and_5 (and_5_out, X_1, not_2_out);
  or \or  (out_5, and_1_out, and_2_out, and_3_out, and_4_out, and_5_out);

  // Notes on the sheet:
  //   X_2
endmodule

module Comparador_completo (
  input  X_1,
  input  in_2,
  input  Y_1,
  input  Y_2,
  output out_5,
  output out_6,
  output out_7
);

  wire and_1_out, and_2_out, and_3_out, and_4_out, and_5_out, and_6_out, and_7_out, and_8_out, and_9_out,
       and_10_out, not_1_out, not_2_out, not_3_out, not_4_out;

  not not_1 (not_1_out, X_1);
  not not_2 (not_2_out, in_2);
  not not_3 (not_3_out, Y_1);
  not not_4 (not_4_out, Y_2);
  and and_1 (and_1_out, in_2, not_3_out, not_4_out);
  and and_2 (and_2_out, X_1, in_2, not_4_out);
  and and_3 (and_3_out, X_1, not_3_out);
  and and_4 (and_4_out, not_1_out, not_2_out, Y_2);
  and and_5 (and_5_out, not_2_out, Y_1, Y_2);
  and and_6 (and_6_out, not_1_out, Y_1);
  and and_7 (and_7_out, not_1_out, not_2_out, not_3_out, not_4_out);
  and and_8 (and_8_out, not_1_out, in_2, not_3_out, Y_2);
  and and_9 (and_9_out, X_1, in_2, Y_1, Y_2);
  and and_10 (and_10_out, X_1, not_2_out, Y_1, not_4_out);
  or \or  (out_5, and_1_out, and_2_out, and_3_out);
  or or_2 (out_6, and_4_out, and_5_out, and_6_out);
  or or_3 (out_7, and_7_out, and_8_out, and_9_out, and_10_out);

  // Notes on the sheet:
  //   X_2
endmodule
