// Logisim project Practica4-Arquitectura.circ as structural Verilog: 6 circuits, main circuit Half adder
module Multiplexor (
  input  [7:0] Numero_1,
  input  [7:0] Numero_2,
  input  Switch,
  output [7:0] Resultado,
  output Desbordamiento
);

  wire and_1_out, and_2_out, not_1_out, Restador_complemento_a_2, Sumador_desbordamiento;
  wire [7:0] Restador_out_3, Sumador_out_3;

  Sumador Sumador (.in_1(Numero_1), .in_2(Numero_2), .Desbordamiento(Sumador_desbordamiento), .out_3(Sumador_out_3));
  Restador Restador (
    .in_1(Numero_1), .in_2(Numero_2), .Complemento_a_2(Restador_complemento_a_2), .out_3(Restador_out_3));
  Multiplexer #(.width(8)) multiplexer_1 (
    .in0(Sumador_out_3), .in1(Restador_out_3), .out(Resultado), .sel(Switch));  // open: en
  not not_1 (not_1_out, Switch);
  and and_1 (and_1_out, not_1_out, Sumador_desbordamiento);
  or or_1 (Desbordamiento, and_1_out, and_2_out);
  and and_2 (and_2_out, Switch, Restador_complemento_a_2);

  // Notes on the sheet:
  //   +
  //   0 Sumador
  //   1 Restador
endmodule

module Subcircuito_extra (
  input  _0_Suma,
  input  [7:0] _1_Resta,
  input  [7:0] in_3,
  input  [7:0] in_4,
  input  [7:0] in_5
);

  wire multiplexor_1_desbordamiento;

  Multiplexor multiplexor_1 (
    .Numero_1(_1_Resta), .Numero_2(in_4), .Switch(_0_Suma), .Resultado(in_5),
    .Desbordamiento(multiplexor_1_desbordamiento));
endmodule

module Sumador (
  input  [7:0] in_1,
  input  [7:0] in_2,
  output [7:0] out_3,
  output Desbordamiento
);

  wire full_adder_1_acarreo, full_adder_2_acarreo, full_adder_3_acarreo, full_adder_4_acarreo,
       full_adder_5_acarreo, full_adder_6_acarreo, half_adder_1_acarreo;

  Full_adder full_adder_1 (
    .X(in_1[1]), .Carreo(half_adder_1_acarreo), .y(in_2[1]), .Acarreo(full_adder_1_acarreo), .Suma(out_3[1]));
  Half_adder half_adder_1 (.X(in_1[0]), .Y(in_2[0]), .Acarreo(half_adder_1_acarreo), .Suma(out_3[0]));
  Full_adder full_adder_2 (
    .X(in_1[2]), .Carreo(full_adder_1_acarreo), .y(in_2[2]), .Acarreo(full_adder_2_acarreo), .Suma(out_3[2]));
  Full_adder full_adder_3 (
    .X(in_1[3]), .Carreo(full_adder_2_acarreo), .y(in_2[3]), .Acarreo(full_adder_3_acarreo), .Suma(out_3[3]));
  Full_adder full_adder_4 (
    .X(in_1[4]), .Carreo(full_adder_3_acarreo), .y(in_2[4]), .Acarreo(full_adder_4_acarreo), .Suma(out_3[4]));
  Full_adder full_adder_5 (
    .X(in_1[5]), .Carreo(full_adder_4_acarreo), .y(in_2[5]), .Acarreo(full_adder_5_acarreo), .Suma(out_3[5]));
  Full_adder full_adder_6 (
    .X(in_1[6]), .Carreo(full_adder_5_acarreo), .y(in_2[6]), .Acarreo(full_adder_6_acarreo), .Suma(out_3[6]));
  Full_adder full_adder_7 (
    .X(in_1[7]), .Carreo(full_adder_6_acarreo), .y(in_2[7]), .Acarreo(Desbordamiento), .Suma(out_3[7]));

  // Notes on the sheet:
  //   Numero 1 
  //   +
  //   Numero 2
  //   Resultado
endmodule

module Restador (
  input  [7:0] in_1,
  input  [7:0] in_2,
  output [7:0] out_3,
  output Complemento_a_2
);

  wire full_adder_1_acarreo, full_adder_2_acarreo, full_adder_3_acarreo, full_adder_4_acarreo,
       full_adder_5_acarreo, full_adder_6_acarreo, full_adder_7_acarreo, full_adder_8_acarreo, not_1_out,
       not_2_out, not_3_out, not_4_out, not_5_out, not_6_out, not_7_out, not_8_out;

  not not_1 (not_1_out, in_2[0]);
  not not_2 (not_2_out, in_2[1]);
  not not_3 (not_3_out, in_2[2]);
  not not_4 (not_4_out, in_2[3]);
  not not_5 (not_5_out, in_2[4]);
  not not_6 (not_6_out, in_2[5]);
  not not_7 (not_7_out, in_2[6]);
  not not_8 (not_8_out, in_2[7]);
  not not_9 (Complemento_a_2, full_adder_8_acarreo);
  Full_adder full_adder_1 (
    .X(in_1[1]), .Carreo(full_adder_2_acarreo), .y(not_2_out), .Acarreo(full_adder_1_acarreo), .Suma(out_3[1]));
  Full_adder full_adder_2 (.X(1'b1), .Carreo(in_1[0]), .y(not_1_out), .Acarreo(full_adder_2_acarreo), .Suma(out_3[0]));
  Full_adder full_adder_3 (
    .X(in_1[2]), .Carreo(full_adder_1_acarreo), .y(not_3_out), .Acarreo(full_adder_3_acarreo), .Suma(out_3[2]));
  Full_adder full_adder_4 (
    .X(in_1[3]), .Carreo(full_adder_3_acarreo), .y(not_4_out), .Acarreo(full_adder_4_acarreo), .Suma(out_3[3]));
  Full_adder full_adder_5 (
    .X(in_1[4]), .Carreo(full_adder_4_acarreo), .y(not_5_out), .Acarreo(full_adder_5_acarreo), .Suma(out_3[4]));
  Full_adder full_adder_6 (
    .X(in_1[5]), .Carreo(full_adder_5_acarreo), .y(not_6_out), .Acarreo(full_adder_6_acarreo), .Suma(out_3[5]));
  Full_adder full_adder_7 (
    .X(in_1[6]), .Carreo(full_adder_6_acarreo), .y(not_7_out), .Acarreo(full_adder_7_acarreo), .Suma(out_3[6]));
  Full_adder full_adder_8 (
    .X(in_1[7]), .Carreo(full_adder_7_acarreo), .y(not_8_out), .Acarreo(full_adder_8_acarreo), .Suma(out_3[7]));

  // Notes on the sheet:
  //   Numero 1 
  //   -
  //   Numero 2
  //   Resultado
endmodule

module Full_adder (
  input  X,
  input  Carreo,
  input  y,
  output Acarreo,
  output Suma
);

  wire half_adder_1_acarreo, half_adder_1_suma, half_adder_2_acarreo;

  Half_adder half_adder_1 (.X(X), .Y(Carreo), .Acarreo(half_adder_1_acarreo), .Suma(half_adder_1_suma));
  Half_adder half_adder_2 (.X(half_adder_1_suma), .Y(y), .Acarreo(half_adder_2_acarreo), .Suma(Suma));
  or or_1 (Acarreo, half_adder_1_acarreo, half_adder_2_acarreo);
endmodule

module Half_adder (
  input  X,
  input  Y,
  output Acarreo,
  output Suma
);

  and and_1 (Acarreo, X, Y);
  xor xor_1 (Suma, X, Y);
endmodule
