// Logisim project Practica5.circ as structural Verilog: 3 circuits, main circuit main
module main (
  input  IN,
  input  Hex
);

  wire [1:0] n1_automata_1_q2;

  _1__Automata u_1_automata_1 (.Q1(n1_automata_1_q2[1]), .Q2(n1_automata_1_q2[0]), .In(IN));
  Hex_Digit_Display hex_digit_display_1 (.value({{2{Hex}}, n1_automata_1_q2}));  // open: dp
endmodule

module Flip_Flop_SR (
  input  S,
  input  R,
  output Q,
  output Q_prime
);

  wire and_1_out, and_2_out, clock_1_out;

  Clock clock_1 (.out(clock_1_out));
  and and_1 (and_1_out, S, clock_1_out);
  and and_2 (and_2_out, clock_1_out, R);
  nor nor_1 (Q, and_1_out, Q_prime);
  nor nor_2 (Q_prime, Q, and_2_out);
endmodule

// Aut
module _1__Automata (
  input  In,
  output Q1,
  output Q2
);

  wire and_1_out, and_2_out, and_3_out, clock_1_out, not_1_out, not_2_out, not_3_out;

  not not_1 (not_1_out, In);
  not not_2 (not_2_out, Q1);
  Clock clock_1 (.out(clock_1_out));
  not not_3 (not_3_out, Q2);
  and and_1 (and_1_out, not_1_out, Q2, not_2_out);
  and and_2 (and_2_out, not_1_out, Q2, Q1);
  and and_3 (and_3_out, not_3_out, not_1_out);
  J_K_Flip_Flop j_k_ff_1 (.J(and_1_out), .clk(clock_1_out), .K(and_2_out), .Q(Q1));  // open: Qn, preset, en, reset
  J_K_Flip_Flop j_k_ff_2 (.J(and_3_out), .clk(clock_1_out), .K(Q2), .Q(Q2));  // open: Qn, preset, en, reset
endmodule
