// Logisim project Practica5.circ as structural Verilog: 7 circuits, main circuit main
module main (
  input  [7:0] In,
  input  In_2,
  input  Reset,
  input  Enable,
  input  Hex,
  input  [7:0] Escribir_Datos,
  input  [1:0] Escribir_Datos_2,
  input  [15:0] \Codigo_de_Operación ,
  input  Escribir,
  input  [1:0] Leer_Registro_1,
  input  _0_Leer___1_Escribir,
  input  [1:0] Leer_Registro_2,
  output [7:0] Out,
  output [7:0] Leer_Dato_1,
  output [7:0] Leer_Dato_2,
  output [7:0] Registro_1,
  output [7:0] Registro_2
);

  wire clock_1_out;
  wire [1:0] n1_automata_1_q2;

  _1__Automata u_1_automata_1 (.Q1(n1_automata_1_q2[1]), .Q2(n1_automata_1_q2[0]), .In(In_2));
  Hex_Digit_Display hex_digit_display_1 (.value({{2{Hex}}, n1_automata_1_q2}));  // open: dp
  _3__Banco_de_Registros u_3_banco_de_registros_1 (
    .Escribir_Datos(Escribir_Datos), .Escribir(Escribir), .Leer_Dato_1(Leer_Dato_1),
    .Leer_Dato_2(Leer_Dato_2), .Escribir_Registro(Escribir_Datos_2), .Leer_Registro_1(Leer_Registro_1),
    .Leer_Registro_2(Leer_Registro_2));
  Clock clock_1 (.out(clock_1_out));
  _2__Registro u_2_registro_1 (.Entrada(In), .Enable(Enable), .Reset(Reset), .out_5(Out), .Reloj(clock_1_out));
  _4__Banco_de_Datos u_4_banco_de_datos_1 (
    .\Codigo_de_Operación (\Codigo_de_Operación ), ._0_Leer___1_Escribir(_0_Leer___1_Escribir),
    .Registro_1(Registro_2), .Registro_2(Registro_1));

  // Notes on the sheet:
  //   1) Automata
  //   3) Banco de Registros
  //   2) Registro
  //   4) Banco de Datos
  //   El registro 1 muestra la dirección del bit 5-6 del codigo de Operación
  //   Y el registro 2, muestra la dirección del bit 7-8 del codigo de Operación
  //   Para que empiece a funcionar, debemos de poner en el estado 1 el boton de leer/escribir
endmodule

module _4__Banco_de_Datos (
  input  [15:0] \Codigo_de_Operación ,
  input  _0_Leer___1_Escribir,
  output [7:0] Registro_1,
  output [7:0] Registro_2
);

  wire [7:0] adder_1_out, multiplexer_1_out, multiplexer_2_out, subtractor_1_out;

  _3__Banco_de_Registros u_3_banco_de_registros_1 (
    .Escribir_Datos(multiplexer_2_out), .Escribir(_0_Leer___1_Escribir), .Leer_Dato_1(Registro_1),
    .Leer_Dato_2(Registro_2), .Escribir_Registro({\Codigo_de_Operación [12], \Codigo_de_Operación [13]}),
    .Leer_Registro_1({\Codigo_de_Operación [10], \Codigo_de_Operación [11]}),
    .Leer_Registro_2({\Codigo_de_Operación [8], \Codigo_de_Operación [9]}));
  Multiplexer #(.width(8), .enable("false")) multiplexer_1 (
    .in0(Registro_2), .in1(\Codigo_de_Operación [7:0]), .out(multiplexer_1_out),
    .sel(\Codigo_de_Operación [14]));
  Adder adder_1 (.a(Registro_1), .b(multiplexer_1_out), .out(adder_1_out));  // open: cin, cout
  Subtractor subtractor_1 (.a(Registro_1), .b(multiplexer_1_out), .out(subtractor_1_out));  // open: bin, bout
  Multiplexer #(.width(8), .enable("false")) multiplexer_2 (
    .in0(adder_1_out), .in1(subtractor_1_out), .out(multiplexer_2_out), .sel(\Codigo_de_Operación [15]));
endmodule

module _3__Banco_de_Registros (
  input  [1:0] Leer_Registro_1,
  input  [7:0] Escribir_Datos,
  input  [1:0] Escribir_Registro,
  input  [1:0] Leer_Registro_2,
  input  Escribir,
  output [7:0] Leer_Dato_1,
  output [7:0] Leer_Dato_2
);

  wire Reloj_out;
  wire [7:0] demultiplexer_1_out0, demultiplexer_1_out1, demultiplexer_1_out2, demultiplexer_1_out3,
       n2_registro_1_out_5, n2_registro_2_out_5, n2_registro_3_out_5, n2_registro_4_out_5;

  Demultiplexer #(.select(2), .width(8), .tristate("true"), .enable("false")) demultiplexer_1 (
    .out0(demultiplexer_1_out0), .out1(demultiplexer_1_out1), .out2(demultiplexer_1_out2),
    .out3(demultiplexer_1_out3), .in(Escribir_Datos), .sel(Escribir_Registro));
  Clock Reloj (.out(Reloj_out));
  _2__Registro u_2_registro_1 (
    .Entrada(demultiplexer_1_out0), .Enable(Escribir), .out_5(n2_registro_1_out_5), .Reloj(Reloj_out));  // open: Reset
  _2__Registro u_2_registro_2 (
    .Entrada(demultiplexer_1_out1), .Enable(Escribir), .out_5(n2_registro_2_out_5), .Reloj(Reloj_out));  // open: Reset
  _2__Registro u_2_registro_3 (
    .Entrada(demultiplexer_1_out2), .Enable(Escribir), .out_5(n2_registro_3_out_5), .Reloj(Reloj_out));  // open: Reset
  _2__Registro u_2_registro_4 (
    .Entrada(demultiplexer_1_out3), .Enable(Escribir), .out_5(n2_registro_4_out_5), .Reloj(Reloj_out));  // open: Reset
  Multiplexer #(.select(2), .width(8), .enable("false")) multiplexer_1 (
    .in0(n2_registro_1_out_5), .in1(n2_registro_2_out_5), .in2(n2_registro_3_out_5),
    .in3(n2_registro_4_out_5), .out(Leer_Dato_1), .sel(Leer_Registro_1));
  Multiplexer #(.select(2), .width(8), .enable("false")) multiplexer_2 (
    .in0(n2_registro_1_out_5), .in1(n2_registro_2_out_5), .in2(n2_registro_3_out_5),
    .in3(n2_registro_4_out_5), .out(Leer_Dato_2), .sel(Leer_Registro_2));
endmodule

// Reg
module _2__Registro (
  input  [7:0] Entrada,
  input  Reloj,
  input  Enable,
  input  Reset,
  output [7:0] out_5
);

  D_Flip_Flop d_ff_1 (.clk(Reloj), .D(Entrada[7]), .Q(out_5[7]), .en(Enable), .reset(Reset));  // open: Qn, preset
  D_Flip_Flop d_ff_2 (.clk(Reloj), .D(Entrada[6]), .Q(out_5[6]), .en(Enable), .reset(Reset));  // open: Qn, preset
  D_Flip_Flop d_ff_3 (.clk(Reloj), .D(Entrada[5]), .Q(out_5[5]), .en(Enable), .reset(Reset));  // open: Qn, preset
  D_Flip_Flop d_ff_4 (.clk(Reloj), .D(Entrada[4]), .Q(out_5[4]), .en(Enable), .reset(Reset));  // open: Qn, preset
  D_Flip_Flop d_ff_5 (.clk(Reloj), .D(Entrada[3]), .Q(out_5[3]), .en(Enable), .reset(Reset));  // open: Qn, preset
  D_Flip_Flop d_ff_6 (.clk(Reloj), .D(Entrada[2]), .Q(out_5[2]), .en(Enable), .reset(Reset));  // open: Qn, preset
  D_Flip_Flop d_ff_7 (.clk(Reloj), .D(Entrada[1]), .Q(out_5[1]), .en(Enable), .reset(Reset));  // open: Qn, preset
  D_Flip_Flop d_ff_8 (.clk(Reloj), .D(Entrada[0]), .Q(out_5[0]), .en(Enable), .reset(Reset));  // open: Qn, preset
endmodule

// Aut
module _1__Automata (
  input  In,
  output Q1,
  output Q2
);

  wire and_1_out, and_2_out, and_3_out, clock_1_out, not_1_out, not_2_out, not_3_out;

  not not_1 (not_1_out, In);
  not not_2 (not_2_out, Q1);
  Clock clock_1 (.out(clock_1_out));
  not not_3 (not_3_out, Q2);
  and and_1 (and_1_out, not_1_out, Q2, not_2_out);
  and and_2 (and_2_out, not_1_out, Q2, Q1);
  and and_3 (and_3_out, not_3_out, not_1_out);
  J_K_Flip_Flop j_k_ff_1 (.J(and_1_out), .clk(clock_1_out), .K(and_2_out), .Q(Q1));  // open: Qn, preset, en, reset
  J_K_Flip_Flop j_k_ff_2 (.J(and_3_out), .clk(clock_1_out), .K(Q2), .Q(Q2));  // open: Qn, preset, en, reset
endmodule

module Flip_Flop_SR (
  input  S,
  input  R,
  output Q,
  output Q_prime
);

  wire and_1_out, and_2_out, clock_1_out;

  Clock clock_1 (.out(clock_1_out));
  and and_1 (and_1_out, S, clock_1_out);
  and and_2 (and_2_out, clock_1_out, R);
  nor nor_1 (Q, and_1_out, Q_prime);
  nor nor_2 (Q_prime, Q, and_2_out);
endmodule

module Flip_Flop_D (
  input  D,
  output Q,
  output Q_prime
);

  wire and_1_out, and_2_out, clock_1_out, not_1_out;

  Clock clock_1 (.out(clock_1_out));
  not not_1 (not_1_out, D);
  and and_1 (and_1_out, not_1_out, clock_1_out);
  and and_2 (and_2_out, clock_1_out, D);
  nor nor_1 (Q, and_1_out, Q_prime);
  nor nor_2 (Q_prime, Q, and_2_out);
endmodule
